# Fritzing sketch DrinkMachine (saved by Fritzing 0.9.3b)

parts:
  Raspberry_Pi_1 = Raspberry Pi 3 [part_number=RPI-3-V1.2]
  8_Channel_Relay1 = 8 Channel Power Relay
  M3 = DC Motor
  M5 = DC Motor
  M6 = DC Motor
  M7 = DC Motor
  M8 = DC Motor
  M9 = DC Motor
  M10 = DC Motor
  M4 = DC Motor
  Part1 = LCD1602-I2C

nets:
  N1: Raspberry_Pi_1.GPIO2, Part1.SDA
  N2: Raspberry_Pi_1.GPIO3, Part1.SCL
  N3: Raspberry_Pi_1.GPIO7, 8_Channel_Relay1.IN1
  N4: Raspberry_Pi_1.GPIO8, 8_Channel_Relay1.IN2
  N5: Raspberry_Pi_1.GPIO25, 8_Channel_Relay1.IN3
  N6: Raspberry_Pi_1.GPIO24, 8_Channel_Relay1.IN4
  N7: Raspberry_Pi_1.GPIO23, 8_Channel_Relay1.IN5
  GND: Raspberry_Pi_1.GND, 8_Channel_Relay1.GND, Part1.GND
  N8: Raspberry_Pi_1.GPIO18, 8_Channel_Relay1.IN6
  N9: Raspberry_Pi_1.GPIO15, 8_Channel_Relay1.IN7
  N10: Raspberry_Pi_1.GPIO14, 8_Channel_Relay1.IN8
  5V: Raspberry_Pi_1.5V, 8_Channel_Relay1.VCC#17, Part1.VCC
  N11: 8_Channel_Relay1.VCC#19, 8_Channel_Relay1.JD-VCC
  N12: M3.pin_2, M5.pin_2, M6.pin_2, M7.pin_2, M8.pin_2, M9.pin_2, M10.pin_2, M4.pin_2

notes:
  12v power supply
  12v to 5v converter sends pwr to pi

custom parts:
  8 Channel Power Relay: An 8 channel power relay. The module operates at 5V.
  LCD1602-I2C: A standard character display, usually with 2x16 characters. Comes in many colors with LCM1602 IIC attached.
