# Fritzing sketch DrinkMachine_AllGPIO (saved by Fritzing 0.9.3b)
breadboards: 1

parts:
  Raspberry_Pi_1 = Raspberry Pi 3 [part_number=RPI-3-V1.2]
  U1 = LCD-16X2 [package=lcd-16x2]
  U2 = POT [package=alps_pot]
  U3 = POT [package=alps_pot]
  D1 = Diode [package=diode-1n4148]
  8_Channel_Relay1 = 8 Channel Power Relay
  M3 = DC Motor
  M5 = DC Motor
  M6 = DC Motor
  M7 = DC Motor
  M8 = DC Motor
  M9 = DC Motor
  M10 = DC Motor
  M4 = DC Motor

nets:
  N1: Raspberry_Pi_1.ID_SD, U1.DB7
  N2: Raspberry_Pi_1.GPIO5, U1.DB6
  N3: Raspberry_Pi_1.GPIO6, U1.DB5
  N4: Raspberry_Pi_1.GPIO13, U1.DB4
  N5: Raspberry_Pi_1.GPIO19, U1.E
  N6: Raspberry_Pi_1.GPIO26, U1.RS
  N7: Raspberry_Pi_1.GPIO7, 8_Channel_Relay1.IN1
  N8: Raspberry_Pi_1.GPIO8, 8_Channel_Relay1.IN2
  N9: Raspberry_Pi_1.GPIO25, 8_Channel_Relay1.IN3
  N10: Raspberry_Pi_1.GPIO24, 8_Channel_Relay1.IN4
  N11: Raspberry_Pi_1.GPIO23, 8_Channel_Relay1.IN5
  GND: Raspberry_Pi_1.GND, U1.VSS, U1.R_W, U1.K, U2.A, 8_Channel_Relay1.GND
  N12: Raspberry_Pi_1.GPIO18, 8_Channel_Relay1.IN6
  N13: Raspberry_Pi_1.GPIO15, 8_Channel_Relay1.IN7
  N14: Raspberry_Pi_1.GPIO14, 8_Channel_Relay1.IN8
  N15: Raspberry_Pi_1.5V, U3.E, 8_Channel_Relay1.VCC#17
  N16: U1.VDD, D1.C
  N17: U1.VO, U2.S
  N18: U1.A, U3.S
  N19: 8_Channel_Relay1.VCC#19, 8_Channel_Relay1.JD-VCC
  N20: M3.pin_2, M5.pin_2, M6.pin_2, M7.pin_2, M8.pin_2, M9.pin_2, M10.pin_2, M4.pin_2

notes:
  12v power supply
  12v to 5v converter sends pwr to pi

custom parts:
  8 Channel Power Relay: An 8 channel power relay. The module operates at 5V.
